// Logisim project CPU-Modified-PC.circ as structural Verilog: 3 circuits, main circuit main
module main (
  input  [3:0] in_1,
  input  in_2,
  output [7:0] out_3
);

  wire main_1_p1, main_1_p3, main_2_out_2, main_2_out_3, main_2_out_4, main_2_out_5, main_2_out_6,
       main_2_out_7, main_2_out_8, main_3_out_2, main_3_out_3, main_3_out_4, main_3_out_5, main_3_out_6,
       main_3_out_7, main_3_out_8, main_4_out_2, main_4_out_3, main_4_out_4, main_4_out_5, main_4_out_6,
       main_4_out_7, main_4_out_8;
  wire [3:0] adder_1_out, multiplexer_1_out, register_1_q, yeah_1_out_21, yeah_1_out_22, yeah_1_out_23;
  wire [7:0] adder_2_out, register_2_q;

  // _4BitCounter_main main_1: pin names not known; wires that end beside it: main_1_p1, main_1_p1, main_1_p3, in_1
  Clock clock_1 (.out(main_1_p1));
  Multiplexer #(.width(4)) multiplexer_1 (
    .in0(4'b0000), .in1(4'b0001), .out(multiplexer_1_out), .sel(main_1_p3));  // open: en
  Adder #(.width(4)) adder_1 (.a(multiplexer_1_out), .b(register_1_q), .out(adder_1_out));  // open: cin, cout
  Adder adder_2 (.a(register_2_q), .b(8'h7), .out(adder_2_out));  // open: cin, cout
  Register #(.width(4)) register_1 (.D(adder_1_out), .Q(register_1_q), .clk(main_1_p1));  // open: en, clr
  Register register_2 (.D(adder_2_out), .Q(register_2_q), .clk(main_1_p1));  // open: en, clr
  RAM RAM (.in_3(register_2_q), .in_1(in_2), .in_2(main_1_p1), .out_5(out_3), .in_4(register_1_q));
  _7_Segment_Display u_7_segment_display_1 (
    .g(main_2_out_2), .f(main_2_out_3), .a(main_2_out_4), .b(main_2_out_5), .e(main_2_out_8),
    .d(main_2_out_7), .c(main_2_out_6));  // open: dp
  display_main main_2 (
    .in_1(yeah_1_out_23), .out_6(main_2_out_6), .out_7(main_2_out_7), .out_8(main_2_out_8),
    .out_2(main_2_out_2), .out_3(main_2_out_3), .out_4(main_2_out_4), .out_5(main_2_out_5));
  _7_Segment_Display u_7_segment_display_2 (
    .g(main_3_out_2), .f(main_3_out_3), .a(main_3_out_4), .b(main_3_out_5), .e(main_3_out_8),
    .d(main_3_out_7), .c(main_3_out_6));  // open: dp
  Yeah yeah_1 (
    .in_1(1'b0), .in_2(1'b0), .in_3(1'b0), .in_4(1'b0), .in_5(1'b0), .in_6(1'b0), .in_7(1'b0), .in_8(1'b0),
    .in_9(1'b0), .in_10(1'b0), .in_11(1'b0), .in_12(1'b0), .in_13(out_3[7]), .in_14(out_3[6]),
    .in_15(out_3[5]), .in_16(out_3[4]), .in_17(out_3[3]), .in_18(out_3[2]), .in_19(out_3[1]),
    .in_20(out_3[0]), .out_21(yeah_1_out_21), .out_22(yeah_1_out_22), .out_23(yeah_1_out_23));
  display_main main_3 (
    .in_1(yeah_1_out_22), .out_6(main_3_out_6), .out_7(main_3_out_7), .out_8(main_3_out_8),
    .out_2(main_3_out_2), .out_3(main_3_out_3), .out_4(main_3_out_4), .out_5(main_3_out_5));
  _7_Segment_Display u_7_segment_display_3 (
    .g(main_4_out_2), .f(main_4_out_3), .a(main_4_out_4), .b(main_4_out_5), .e(main_4_out_8),
    .d(main_4_out_7), .c(main_4_out_6));  // open: dp
  display_main main_4 (
    .in_1(yeah_1_out_21), .out_6(main_4_out_6), .out_7(main_4_out_7), .out_8(main_4_out_8),
    .out_2(main_4_out_2), .out_3(main_4_out_3), .out_4(main_4_out_4), .out_5(main_4_out_5));
endmodule

module ADD (
  input  [7:0] in_1,
  input  in_2,
  input  ITEM_5,
  input  ITEM_4,
  input  in_5,
  input  in_6,
  input  ITEM_2,
  input  in_8,
  input  in_9,
  input  in_10,
  output out_11
);

  wire and_1_out, and_2_out, and_3_out, and_4_out, clock_1_out, decoder_1_out0, decoder_1_out1,
       decoder_2_out0, decoder_2_out1;
  wire [7:0] adder_1_out_5, multiplexer_1_out, multiplexer_2_out, multiplexer_3_out, register_1_q,
       register_2_q, register_3_q, register_4_q, register_5_q;

  Multiplexer #(.width(8)) multiplexer_1 (
    .in0(in_1), .in1(register_5_q), .out(multiplexer_1_out), .sel(in_8));  // open: en
  Register register_1 (.D(multiplexer_1_out), .Q(register_1_q), .clk(and_1_out));  // open: en, clr
  and and_1 (and_1_out, decoder_1_out0, ITEM_5, clock_1_out);
  Decoder decoder_1 (.out0(decoder_1_out0), .out1(decoder_1_out1), .sel(ITEM_4));  // open: en
  Clock clock_1 (.out(clock_1_out));
  Register register_2 (.D(multiplexer_1_out), .Q(register_2_q), .clk(and_2_out));  // open: en, clr
  and and_2 (and_2_out, decoder_1_out1, ITEM_5, clock_1_out);
  Multiplexer #(.width(8)) multiplexer_2 (
    .in0(register_1_q), .in1(register_2_q), .out(multiplexer_2_out), .sel(in_5));  // open: en
  Multiplexer #(.width(8)) multiplexer_3 (
    .in0(multiplexer_1_out), .in1(multiplexer_2_out), .out(multiplexer_3_out), .sel(in_6));  // open: en
  Register register_3 (.D(multiplexer_3_out), .Q(register_3_q), .clk(and_3_out));  // open: en, clr
  and and_3 (and_3_out, clock_1_out, decoder_2_out0, decoder_2_out0);
  Decoder decoder_2 (.out0(decoder_2_out0), .out1(decoder_2_out1), .sel(ITEM_2));  // open: en
  Register register_4 (.D(multiplexer_3_out), .Q(register_4_q), .clk(and_4_out));  // open: en, clr
  and and_4 (and_4_out, clock_1_out, decoder_2_out1, decoder_2_out1);
  ADDER adder_1 (.in_1(in_2), .in_2(register_3_q), .in_3(register_4_q), .out_4(out_11), .out_5(adder_1_out_5));
  Register register_5 (.D(adder_1_out_5), .Q(register_5_q), .clk(clock_1_out));  // open: en, clr

  // Notes on the sheet:
  //   ITEM 1
  //   ITEM 3
  //   A-OUT
endmodule

module CONTROL_UNIT (
  input  [7:0] in_1,
  output out_2,
  output out_3,
  output out_4,
  output out_5,
  output out_6,
  output out_7,
  output out_8,
  output out_9,
  output out_10,
  output out_11
);

  wire _00, _01, _10, _11, add, ARG1, ARG2, CLK, DEST, INP, not_1_out, not_2_out, not_3_out, not_4_out,
       not_5_out, not_6_out, not_7_out, not_8_out, not_9_out, not_10_out, not_11_out, not_12_out, not_13_out,
       not_14_out, not_15_out, or_1_out, or_2_out, PRT, STP, SUB;
  wire [3:0] _1TK, _3TX, _4TX, adder_1_out, or_3_out;
  wire [7:0] multiplexer_3_out, multiplexer_5_out;

  Clock clock_1 (.out(CLK));
  not not_1 (not_1_out, multiplexer_5_out[2]);
  not not_2 (not_2_out, multiplexer_5_out[1]);
  not not_3 (not_3_out, multiplexer_5_out[0]);
  not not_4 (not_4_out, multiplexer_5_out[1]);
  not not_5 (not_5_out, multiplexer_5_out[2]);
  not not_6 (not_6_out, multiplexer_5_out[3]);
  and u_ADD (add, multiplexer_5_out[3], not_1_out, not_2_out, not_3_out);
  and u_SUB (SUB, not_6_out, not_5_out, not_4_out, multiplexer_5_out[0]);
  not not_7 (not_7_out, multiplexer_5_out[0]);
  not not_8 (not_8_out, multiplexer_5_out[3]);
  not not_9 (not_9_out, multiplexer_5_out[3]);
  and u_PRT (PRT, not_9_out, not_8_out, multiplexer_5_out[1], not_7_out);
  or or_1 (or_1_out, SUB, add);
  or or_2 (or_2_out, PRT, INP);
  and and_1 (out_10, not_13_out, _01);
  not not_10 (not_10_out, multiplexer_5_out[3]);
  not not_11 (not_11_out, multiplexer_5_out[0]);
  not not_12 (not_12_out, multiplexer_5_out[3]);
  and u_STP (STP, not_12_out, multiplexer_5_out[2], multiplexer_5_out[1], not_11_out);
  Multiplexer #(.width(4)) multiplexer_1 (.in0(4'b0000), .in1(4'b0100), .out(_4TX), .sel(or_1_out));  // open: en
  Multiplexer #(.width(4)) multiplexer_2 (.in0(4'b0000), .in1(4'b0001), .out(_1TK), .sel(or_2_out));  // open: en
  not not_13 (not_13_out, multiplexer_3_out[0]);
  and and_2 (out_11, multiplexer_3_out[0], _01);
  not not_14 (not_14_out, multiplexer_5_out[0]);
  not not_15 (not_15_out, multiplexer_5_out[1]);
  and u_INP (INP, not_10_out, multiplexer_5_out[2], not_15_out, not_14_out);
  Multiplexer #(.width(8)) multiplexer_3 (
    .in0({8{1'b0}}), .in1(in_1), .out({multiplexer_3_out[7:6], DEST, multiplexer_3_out[4:0]}), .sel(_01));  // open: en
  Multiplexer #(.width(4)) multiplexer_4 (.in0(4'b0000), .in1(4'b0011), .out(_3TX), .sel(_01));  // open: en
  Multiplexer #(.width(8)) multiplexer_5 (
    .in0({8{1'b0}}), .in1(in_1), .out({multiplexer_5_out[7:6], ARG2, ARG1, multiplexer_5_out[3:0]}), .sel(_00));  // open: en
  assign or_3_out = _4TX | _1TK | _3TX;  // OR_Gate or_3, 4 bits wide
  // AND_Gate and_3 is placed but not wired
  Decoder #(.select(2)) decoder_1 (.out0(_00), .out1(_01), .out2(_10), .out3(_11), .sel(in_1[7:6]));  // open: en
  Adder #(.width(4)) adder_1 (.a(4'b0011), .b(or_3_out), .out(adder_1_out));  // open: cin, cout
  // _4BitCounter_main main_1: pin names not known; wires that end beside it: CLK, out_2, out_3, adder_1_out, out_4, STP, out_5, out_6, out_7, out_8
  // AND_Gate and_4 is placed but not wired

  // Other names for the same wires on the sheet: _1 = out_2; _2 = out_3; _3 = out_4; _4 = out_5; _5 = out_6;
  //   _6 = out_7; _7 = out_8; INSTR[7:0] = in_1; LOAD = out_10; STORE = out_11

  // Notes on the sheet:
  //   ADDER PART
  //   MASTER_COUNTER
endmodule
